# Fritzing sketch sh_arduino (saved by Fritzing 0.9.4)
stripboards: 1

parts:
  Часть7 = Arduino Nano (Rev3.0)
  J1_Arduino-INA226 = female pin header, 4 pins [form="♀ (female)" part_number="12V, GND, SDA, SCL"]
  J2_Arduino-Sensors = female pin header, 4 pins [form="♀ (female)" part_number="3V3, GND, SDA, SCL"]
  J3_Arduino_Downstep3V = female pin header, 1 pin [form="♀ (female)" part_number=3V3]
  C1 = Ceramic Capacitor [capacitance=0.1mF voltage=0.1kV package="100 mil [THT, multilayer]"]
  J3_Arduino-Button = female pin header, 2 pins [form="♀ (female)"]
  LED2 = LED - 5mm [color="Red (633nm)" package="5 mm [THT]"]
  J4_Arduino-RPi = female pin header, 4 pins [form="♀ (female)" part_number="5V, GND, GPIO4, PEN"]
  J5_Arduino_Downstep5V = female pin header, 1 pin [form="♀ (female)" part_number=5V]
  R8 = Resistor [tolerance=±5% resistance=47k package=THT]
  Q7 = NPN-Transistor [part_number=PN2222 package="TO92 [THT]"]
  R9 = Resistor [tolerance=±5% resistance=680 package=THT]
  C8 = Ceramic Capacitor [capacitance=0.1mF voltage=0.1kV package="100 mil [THT, multilayer]"]

nets:
  N1: Часть7.GND, J1_Arduino-INA226.pin2, J2_Arduino-Sensors.pin2, C1.0, J3_Arduino-Button.pin1, J4_Arduino-RPi.pin2, Q7.E, C8.0
  N2: Часть7.D6, J3_Arduino-Button.pin2
  N3: Часть7.D8, LED2.anode
  N4: Часть7.D9, R8.Pin_1
  N5: Часть7.VIN, J1_Arduino-INA226.pin1, C1.1
  N6: Часть7.A5, J1_Arduino-INA226.pin4, J2_Arduino-Sensors.pin4
  N7: Часть7.A4, J1_Arduino-INA226.pin3, J2_Arduino-Sensors.pin3
  N8: J2_Arduino-Sensors.pin1, J3_Arduino_Downstep3V.pin1
  N9: LED2.cathode, J4_Arduino-RPi.pin3
  N10: J4_Arduino-RPi.pin1, J5_Arduino_Downstep5V.pin1
  N11: J4_Arduino-RPi.pin4, Q7.C, R9.Pin_0, R9.Pin_1
  N12: R8.Pin_0, Q7.B, C8.1
